// Logisim project cpu_design_circuits.circ as structural Verilog
module _16_bit_register (
  input  INR,
  input  [15:0] IP,
  input  LOAD,
  input  CLR,
  input  clock_pulse,
  output [15:0] OP
);

  wire [15:0] adder_1_out, multiplexer_1_out, multiplexer_2_out, multiplexer_3_out;

  Multiplexer #(.width(16), .enable("false")) multiplexer_1 (
    .in0(multiplexer_2_out), .in1({16{1'b0}}), .out(multiplexer_1_out), .sel(CLR));
  Adder #(.width(16)) adder_1 (.a(OP), .b(16'h1), .out(adder_1_out));  // open: cin, cout
  Multiplexer #(.width(16), .enable("false")) multiplexer_2 (
    .in0(multiplexer_3_out), .in1(IP), .out(multiplexer_2_out), .sel(LOAD));
  Multiplexer #(.width(16), .enable("false")) multiplexer_3 (
    .in0(OP), .in1(adder_1_out), .out(multiplexer_3_out), .sel(INR));
  Register #(.width(16)) register_1 (.D(multiplexer_1_out), .Q(OP), .clk(clock_pulse));  // open: en, clr
endmodule

module _12_bit_register (
  input  INR,
  input  [11:0] IP,
  input  LOAD,
  input  CLR,
  input  clock_pulse,
  output [11:0] OP
);

  wire [11:0] adder_1_out, multiplexer_1_out, multiplexer_2_out, multiplexer_3_out;

  Multiplexer #(.width(12), .enable("false")) multiplexer_1 (
    .in0(multiplexer_2_out), .in1({12{1'b0}}), .out(multiplexer_1_out), .sel(CLR));
  Adder #(.width(12)) adder_1 (.a(OP), .b(12'h1), .out(adder_1_out));  // open: cin, cout
  Multiplexer #(.width(12), .enable("false")) multiplexer_2 (
    .in0(multiplexer_3_out), .in1(IP), .out(multiplexer_2_out), .sel(LOAD));
  Multiplexer #(.width(12), .enable("false")) multiplexer_3 (
    .in0(OP), .in1(adder_1_out), .out(multiplexer_3_out), .sel(INR));
  Register #(.width(12)) register_1 (.D(multiplexer_1_out), .Q(OP), .clk(clock_pulse));  // open: en, clr
endmodule

module datapath (
  output [15:0] Accum_op
);

  wire AC_inr, ac_load, ACclr, alu_1_cout, AR_inr, AR_load, clock_1_out, decoder_1_out0, decoder_1_out1,
       decoder_1_out2, decoder_1_out3, decoder_1_out4, decoder_1_out5, decoder_1_out6, decoder_1_out7,
       decoder_2_out0, decoder_2_out1, decoder_2_out2, decoder_2_out3, decoder_2_out4, decoder_2_out5,
       decoder_2_out6, decoder_2_out7, dr_inr, DR_load, e_clr, e_ip, e_load, E_q, ir_load, mem_load,
       or_1_out, pc_inr, PC_load;
  wire [2:0] alu_sele, time_control_1_opcode, time_control_1_s2s1s0, time_control_1_time_stage;
  wire [11:0] AR_op, PC_op;
  wire [15:0] alu_1_output, DR_op, multiplexer_1_out, n16_bit_register_1_op, ram_1_data;

  ALU alu_1 (
    .Carryin(E_q), .A(Accum_op), .B(DR_op), .S2S1S0(alu_sele), .IR(E_q), .IL(E_q), .Cout(alu_1_cout),
    .Output(alu_1_output));
  _12_bit_register AR (
    .IP(multiplexer_1_out[11:0]), .CLR(1'b0), .LOAD(AR_load), .INR(AR_inr), .OP(AR_op),
    .clock_pulse(clock_1_out));
  _12_bit_register PC (
    .IP(multiplexer_1_out[11:0]), .CLR(1'b0), .LOAD(PC_load), .INR(pc_inr), .OP(PC_op),
    .clock_pulse(clock_1_out));
  _16_bit_register DR (
    .IP(multiplexer_1_out), .CLR(1'b0), .LOAD(DR_load), .INR(dr_inr), .OP(DR_op), .clock_pulse(clock_1_out));
  _16_bit_register AC (
    .IP(alu_1_output), .CLR(ACclr), .LOAD(ac_load), .INR(AC_inr), .OP(Accum_op), .clock_pulse(clock_1_out));
  _16_bit_register u_16_bit_register_1 (
    .IP(multiplexer_1_out), .CLR(1'b0), .LOAD(ir_load), .INR(1'b0), .OP(n16_bit_register_1_op),
    .clock_pulse(clock_1_out));
  RAM #(.addrWidth(12), .dataWidth(16), .bus("separate")) ram_1 (
    .addr(AR_op), .din(multiplexer_1_out), .data(ram_1_data), .str(mem_load), .sel(1'b1), .clk(clock_1_out),
    .ld(1'b1), .clr(1'b0));
  or or_1 (or_1_out, e_ip, alu_1_cout);
  Clock clock_1 (.out(clock_1_out));
  D_Flip_Flop E (.clk(clock_1_out), .D(or_1_out), .Q(E_q), .preset(1'b0), .en(e_load), .reset(e_clr));  // open: Qn
  Multiplexer #(.select(3), .width(16), .enable("false")) multiplexer_1 (
    .in1({4'b0000, AR_op}), .in2({4'b0000, PC_op}), .in3(DR_op), .in4(Accum_op), .in5(n16_bit_register_1_op),
    .in7(ram_1_data), .out(multiplexer_1_out), .sel(time_control_1_s2s1s0));  // open: in0, in6
  time_control time_control_1 (
    .Instruction(n16_bit_register_1_op), .Clock(clock_1_out), .DR(DR_op), .Acc(Accum_op), .E(E_q),
    .time_stage(time_control_1_time_stage), .opcode(time_control_1_opcode), .DR_load(DR_load),
    .memory_load(mem_load), .DR_inr(dr_inr), .AR_load(AR_load), .alu_sele(alu_sele), .AR_inr(AR_inr),
    .AC_load(ac_load), .ir_load(ir_load), .PC_load(PC_load), .AC_inr(AC_inr), .AC_clr(ACclr), .e_ip(e_ip),
    .S2S1S0(time_control_1_s2s1s0), .pc_inr(pc_inr), .e_clr(e_clr), .e_load(e_load));
  Decoder #(.select(3), .enable("false")) decoder_1 (
    .out0(decoder_1_out0), .out1(decoder_1_out1), .out2(decoder_1_out2), .out3(decoder_1_out3),
    .out4(decoder_1_out4), .out5(decoder_1_out5), .out6(decoder_1_out6), .out7(decoder_1_out7),
    .sel(time_control_1_time_stage));
  Decoder #(.select(3), .enable("false")) decoder_2 (
    .out0(decoder_2_out0), .out1(decoder_2_out1), .out2(decoder_2_out2), .out3(decoder_2_out3),
    .out4(decoder_2_out4), .out5(decoder_2_out5), .out6(decoder_2_out6), .out7(decoder_2_out7),
    .sel(time_control_1_opcode));
  LED led_1 (.in(decoder_1_out0));
  LED led_2 (.in(decoder_1_out1));
  LED led_3 (.in(decoder_1_out2));
  LED led_4 (.in(decoder_1_out3));
  LED led_5 (.in(decoder_1_out4));
  LED led_6 (.in(decoder_1_out5));
  LED led_7 (.in(decoder_1_out6));
  LED led_8 (.in(decoder_1_out7));
  LED led_9 (.in(decoder_2_out0));
  LED led_10 (.in(decoder_2_out1));
  LED led_11 (.in(decoder_2_out2));
  LED led_12 (.in(decoder_2_out3));
  LED led_13 (.in(decoder_2_out4));
  LED led_14 (.in(decoder_2_out5));
  LED led_15 (.in(decoder_2_out6));
  LED led_16 (.in(decoder_2_out7));

  // Notes on the sheet:
  //   ir
  //   T0
  //   T1
  //   T2
  //   T3
  //   T4
  //   T5
  //   T6
  //   T7
  //   and
  //   add
  //   lda
  //   sta
  //   bun
  //   bsa
  //   isz
  //   register-reference
endmodule

module ALU (
  input  Carryin,
  input  [15:0] A,
  input  [15:0] B,
  input  [2:0] S2S1S0,
  input  IR,
  input  IL,
  output Cout,
  output [15:0] Output
);

  wire adder_1_cout;
  wire [15:0] adder_1_out, and_1_out, not_1_out;

  assign and_1_out = A & B;  // AND_Gate and_1, 16 bits wide
  assign not_1_out = ~A;  // NOT_Gate not_1, 16 bits wide
  Adder #(.width(16)) adder_1 (.a(A), .b(B), .out(adder_1_out), .cin(Carryin), .cout(adder_1_cout));
  Multiplexer #(.select(3), .width(16), .enable("false")) multiplexer_1 (
    .in0({16{1'b0}}), .in1(and_1_out), .in2(not_1_out), .in3({IR, A[15:1]}), .in4({A[14:0], IL}), .in5(B),
    .in6(adder_1_out), .in7({16{1'b0}}), .out(Output), .sel(S2S1S0));
  Multiplexer #(.select(3), .enable("false")) multiplexer_2 (
    .in0(1'b0), .in1(1'b0), .in2(1'b0), .in3(A[0]), .in4(A[15]), .in5(1'b0), .in6(adder_1_cout), .in7(1'b0),
    .out(Cout), .sel(S2S1S0));
endmodule

module time_control (
  input  [15:0] Instruction,
  input  Clock,
  input  [15:0] DR,
  input  [15:0] Acc,
  input  E,
  output [2:0] opcode,
  output DR_load,
  output [2:0] time_stage,
  output memory_load,
  output DR_inr,
  output AR_load,
  output [2:0] alu_sele,
  output AR_inr,
  output AC_load,
  output ir_load,
  output PC_load,
  output AC_inr,
  output AC_clr,
  output e_ip,
  output [2:0] S2S1S0,
  output pc_inr,
  output e_clr,
  output e_load
);

  wire ac_dr_2_out, ac_dr_3_out, ac_dr_4_out, ac_dr_out, ac_prime_out, and_1_out, and_2_out, and_3_out,
       and_4_out, and_5_out, and_6_out, and_7_out, and_10_out, and_11_out, and_12_out, and_13_out,
       and_14_out, and_15_out, and_16_out, and_17_out, and_18_out, and_19_out, and_21_out, and_22_out,
       and_26_out, and_27_out, and_28_out, and_29_out, and_30_out, and_34_out, AR_inr_2_out, B0, B1, B2, B3,
       B4, B5, B6, B7, B8, B9, B10, B11, D0, D1, D2, D3, D4, D5, D6, D7, dr_2_out, dr_out, E_prime,
       nor_1_out, nor_2_out, not_1_out, not_3_out, not_4_out, not_5_out, or_4_out, or_5_out, or_12_out, r,
       r_1, sc_clear, shl_out, shr_out, T0, T2, T3, T4, T5, T6, T7, X0, X2, X3, X4;

  Counter #(.width(3), .max('h7)) counter_1 (
    .Q(time_stage), .clk(Clock), .clr(sc_clear));  // open: load, D, count, carry
  and and_1 (and_1_out, D7, Instruction[15], T3);
  and u_AR_inr (AR_inr, D5, T4);
  and and_2 (and_2_out, D5, T5);
  and and_3 (and_3_out, D4, T4);
  and and_4 (and_4_out, D2, T5);
  and and_5 (and_5_out, D6, T6);
  Decoder #(.select(3), .enable("false")) decoder_1 (
    .out0(D0), .out1(D1), .out2(D2), .out3(D3), .out4(D4), .out5(D5), .out6(D6), .out7(D7),
    .sel(Instruction[14:12]));
  Decoder #(.select(3), .enable("false")) decoder_2 (
    .out0(T0), .out1(ir_load), .out2(T2), .out3(T3), .out4(T4), .out5(T5), .out6(T6), .out7(T7),
    .sel(time_stage));
  or or_1 (PC_load, and_2_out, and_3_out);
  nor nor_1 (nor_1_out, Acc[0], Acc[1], Acc[2], Acc[3], Acc[4], Acc[5], Acc[6], Acc[7], Acc[9], Acc[10], Acc[11], Acc[12], Acc[13], Acc[14], Acc[15], Acc[8]);
  or or_2 (X3, and_4_out, and_5_out);
  or u_AR_load (AR_load, and_1_out, T2, T0);
  and and_6 (and_6_out, nor_1_out, B2, r);
  not not_1 (not_1_out, Acc[15]);
  and and_7 (and_7_out, not_1_out, B4, r);
  Decoder #(.select(4), .enable("false")) decoder_3 (
    .out0(B0), .out1(B1), .out2(B2), .out3(B3), .out4(B4), .out5(B5), .out6(B6), .out7(B7), .out8(B8),
    .out9(B9), .out10(B10), .out11(B11), .sel(Instruction[3:0]));  // open: out12, out13, out14, out15
  and and_8 (DR_inr, D6, T5);
  and and_9 (X4, D3, T4);
  nor nor_2 (nor_2_out, DR[0], DR[1], DR[2], DR[3], DR[4], DR[5], DR[6], DR[7], DR[9], DR[10], DR[11], DR[12], DR[13], DR[14], DR[15], DR[8]);
  and and_10 (and_10_out, Acc[15], B3, r);
  not not_2 (E_prime, E);
  and and_11 (and_11_out, D6, nor_2_out, T6);
  and and_12 (and_12_out, E_prime, B1, r);
  or or_3 (pc_inr, and_11_out, and_6_out, and_10_out, ir_load, and_12_out, and_7_out);
  not not_3 (not_3_out, D7);
  or or_4 (or_4_out, D3, D5);
  and and_13 (and_13_out, D6, T6);
  and shr (shr_out, r, B7);
  and u_dr (dr_out, D2, T5);
  and ac_prime (ac_prime_out, r, B9);
  and ac_dr (ac_dr_out, D1, T5);
  and shl (shl_out, r, B6);
  and and_14 (and_14_out, D1, T5);
  and and_15 (and_15_out, r, B8);
  and and_16 (and_16_out, not_3_out, Instruction[15], T3);
  or or_5 (or_5_out, D0, D1, D2, D6);
  and and_17 (and_17_out, or_4_out, T4);
  and ac_dr_2 (ac_dr_2_out, D0, T5);
  or S0 (S2S1S0[0], X0, PC_load, X3, T2);
  or S1 (S2S1S0[1], X0, X2, X3);
  or S2 (S2S1S0[2], X0, X4, T2);
  and and_18 (and_18_out, r, B6);
  and and_19 (and_19_out, r, B7);
  and and_20 (DR_load, or_5_out, T4);
  or or_6 (memory_load, and_17_out, and_13_out);
  or or_7 (alu_sele[0], ac_dr_2_out, shr_out, dr_out);
  or or_8 (alu_sele[1], shr_out, ac_prime_out, ac_dr_out);
  or or_9 (alu_sele[2], ac_dr_out, dr_out, shl_out);
  or or_10 (e_load, and_18_out, and_19_out, and_14_out, and_15_out);
  or or_11 (X0, ir_load, and_16_out, DR_load);
  and dr_2 (dr_2_out, D2, T6);
  and ac_dr_3 (ac_dr_3_out, D1, T7);
  and and_21 (and_21_out, D4, T5);
  and and_22 (and_22_out, D6, T7);
  not not_4 (not_4_out, Instruction[15]);
  or or_12 (or_12_out, D0, D1, D2);
  not not_5 (not_5_out, Instruction[15]);
  and and_23 (r_1, D7, not_4_out, T4);
  and and_24 (r, D7, not_5_out, T3);
  and and_25 (e_clr, r, B10);
  and AR_inr_2 (AR_inr_2_out, D5, T4);
  and ac_dr_4 (ac_dr_4_out, D0, T6);
  and and_26 (and_26_out, D3, T5);
  and and_27 (and_27_out, D5, T6);
  and and_28 (and_28_out, or_12_out, T5);
  and and_29 (and_29_out, r, B6);
  and and_30 (and_30_out, r, B7);
  and and_31 (AC_inr, r, B5);
  and and_32 (AC_clr, r, B11);
  and and_33 (e_ip, r, E_prime, B8);
  or or_13 (X2, T0, AR_inr_2_out);
  and and_34 (and_34_out, r, B9);
  or or_14 (sc_clear, dr_2_out, ac_dr_4_out, ac_dr_3_out, and_26_out, and_21_out, and_27_out, and_22_out, r_1);
  or or_15 (AC_load, and_28_out, and_34_out, and_29_out, and_30_out);

  assign opcode = Instruction[14:12];

  // Other names for the same wires on the sheet: I = Instruction[15]; T1 = ir_load; X1 = PC_load; X5 = T2

  // Notes on the sheet:
  //   alu logic
endmodule
